// Logisim project relogio_digital_24h_eld2.circ as structural Verilog: 1 circuit, main circuit main
module main (
);

  wire and_1_out, and_2_out, and_3_out, and_4_out, and_5_out, clock_1_out, not_1_out, or_1_out, or_2_out,
       or_3_out, QUANDO_3_out, QUANDO_4_out, QUANDO_10_out, t_ff_3_qn, t_ff_11_qn, t_ff_12_qn;
  wire [1:0] Hora_mais_significativo;
  wire [3:0] Hora_menos_significativo, Minuto_mais_significativo, Minuto_menos_significativo,
       Segundo_mais_significativo, Segundo_menos_significativo;

  Clock clock_1 (.out(clock_1_out));
  or or_1 (or_1_out, clock_1_out, QUANDO_3_out);
  and and_1 (and_1_out, QUANDO_10_out, not_1_out);
  T_Flip_Flop #(.trigger("falling")) t_ff_1 (
    .T(1'b1), .clk(or_1_out), .Q(Segundo_menos_significativo[0]), .reset(or_2_out));  // open: Qn, preset
  or or_2 (or_2_out, QUANDO_3_out, and_2_out);
  T_Flip_Flop #(.trigger("falling")) t_ff_2 (
    .T(1'b1), .clk(and_2_out), .Q(Segundo_mais_significativo[0]), .reset(and_3_out));  // open: Qn, preset
  T_Flip_Flop #(.trigger("falling")) t_ff_3 (
    .T(1'b1), .clk(and_1_out), .Q(Hora_mais_significativo[0]), .Qn(t_ff_3_qn), .reset(QUANDO_3_out));  // open: preset
  not not_1 (not_1_out, QUANDO_3_out);
  T_Flip_Flop #(.trigger("falling")) t_ff_4 (
    .T(1'b1), .clk(Segundo_menos_significativo[0]), .Q(Segundo_menos_significativo[1]), .reset(or_2_out));  // open: Qn, preset
  T_Flip_Flop #(.trigger("falling")) t_ff_5 (
    .T(1'b1), .clk(Segundo_mais_significativo[0]), .Q(Segundo_mais_significativo[1]), .reset(and_3_out));  // open: Qn, preset
  and QUANDO_3 (QUANDO_3_out, t_ff_3_qn, QUANDO_4_out, Hora_mais_significativo[1]);
  T_Flip_Flop #(.trigger("falling")) t_ff_6 (
    .T(1'b1), .clk(Hora_mais_significativo[0]), .Q(Hora_mais_significativo[1]), .reset(QUANDO_3_out));  // open: Qn, preset
  T_Flip_Flop #(.trigger("falling")) t_ff_7 (
    .T(1'b1), .clk(Segundo_menos_significativo[1]), .Q(Segundo_menos_significativo[2]), .reset(or_2_out));  // open: Qn, preset
  T_Flip_Flop #(.trigger("falling")) t_ff_8 (
    .T(1'b1), .clk(Segundo_mais_significativo[1]), .Q(Segundo_mais_significativo[2]), .reset(and_3_out));  // open: Qn, preset
  T_Flip_Flop #(.trigger("falling")) t_ff_9 (
    .T(1'b1), .clk(Segundo_menos_significativo[2]), .Q(Segundo_menos_significativo[3]), .reset(or_2_out));  // open: Qn, preset
  and and_2 (and_2_out, Segundo_menos_significativo[1], Segundo_menos_significativo[3]);
  T_Flip_Flop #(.trigger("falling")) t_ff_10 (
    .T(1'b1), .clk(Segundo_mais_significativo[2]), .Q(Segundo_mais_significativo[3]), .reset(and_3_out));  // open: Qn, preset
  and and_3 (and_3_out, Segundo_mais_significativo[1], Segundo_mais_significativo[2]);
  T_Flip_Flop #(.trigger("falling")) t_ff_11 (
    .T(1'b1), .clk(and_5_out), .Q(Hora_menos_significativo[0]), .Qn(t_ff_11_qn), .reset(or_3_out));  // open: preset
  or or_3 (or_3_out, QUANDO_3_out, QUANDO_10_out);
  T_Flip_Flop #(.trigger("falling")) t_ff_12 (
    .T(1'b1), .clk(Hora_menos_significativo[0]), .Q(Hora_menos_significativo[1]), .Qn(t_ff_12_qn),
    .reset(or_3_out));  // open: preset
  T_Flip_Flop #(.trigger("falling")) t_ff_13 (
    .T(1'b1), .clk(Hora_menos_significativo[1]), .Q(Hora_menos_significativo[2]), .reset(or_3_out));  // open: Qn, preset
  and QUANDO_4 (QUANDO_4_out, t_ff_11_qn, t_ff_12_qn, Hora_menos_significativo[2]);
  T_Flip_Flop #(.trigger("falling")) t_ff_14 (
    .T(1'b1), .clk(Hora_menos_significativo[2]), .Q(Hora_menos_significativo[3]), .reset(or_3_out));  // open: Qn, preset
  and QUANDO_10 (QUANDO_10_out, Hora_menos_significativo[1], Hora_menos_significativo[3]);
  T_Flip_Flop #(.trigger("falling")) t_ff_15 (
    .T(1'b1), .clk(and_3_out), .Q(Minuto_menos_significativo[0]), .reset(and_4_out));  // open: Qn, preset
  T_Flip_Flop #(.trigger("falling")) t_ff_16 (
    .T(1'b1), .clk(and_4_out), .Q(Minuto_mais_significativo[0]), .reset(and_5_out));  // open: Qn, preset
  T_Flip_Flop #(.trigger("falling")) t_ff_17 (
    .T(1'b1), .clk(Minuto_menos_significativo[0]), .Q(Minuto_menos_significativo[1]), .reset(and_4_out));  // open: Qn, preset
  T_Flip_Flop #(.trigger("falling")) t_ff_18 (
    .T(1'b1), .clk(Minuto_mais_significativo[0]), .Q(Minuto_mais_significativo[1]), .reset(and_5_out));  // open: Qn, preset
  T_Flip_Flop #(.trigger("falling")) t_ff_19 (
    .T(1'b1), .clk(Minuto_menos_significativo[1]), .Q(Minuto_menos_significativo[2]), .reset(and_4_out));  // open: Qn, preset
  T_Flip_Flop #(.trigger("falling")) t_ff_20 (
    .T(1'b1), .clk(Minuto_mais_significativo[1]), .Q(Minuto_mais_significativo[2]), .reset(and_5_out));  // open: Qn, preset
  T_Flip_Flop #(.trigger("falling")) t_ff_21 (
    .T(1'b1), .clk(Minuto_menos_significativo[2]), .Q(Minuto_menos_significativo[3]), .reset(and_4_out));  // open: Qn, preset
  and and_4 (and_4_out, Minuto_menos_significativo[1], Minuto_menos_significativo[3]);
  T_Flip_Flop #(.trigger("falling")) t_ff_22 (
    .T(1'b1), .clk(Minuto_mais_significativo[2]), .Q(Minuto_mais_significativo[3]), .reset(and_5_out));  // open: Qn, preset
  and and_5 (and_5_out, Minuto_mais_significativo[1], Minuto_mais_significativo[2]);
  Hex_Digit_Display hex_digit_display_1 (.value({2'b00, Hora_mais_significativo}));  // open: dp
  Hex_Digit_Display hex_digit_display_2 (.value(Hora_menos_significativo));  // open: dp
  Hex_Digit_Display hex_digit_display_3 (.value(Minuto_mais_significativo));  // open: dp
  Hex_Digit_Display hex_digit_display_4 (.value(Minuto_menos_significativo));  // open: dp
  Hex_Digit_Display hex_digit_display_5 (.value(Segundo_mais_significativo));  // open: dp
  Hex_Digit_Display hex_digit_display_6 (.value(Segundo_menos_significativo));  // open: dp
endmodule
