// Logisim project relogio_digital_24h_eld2_BLOCKS.circ as structural Verilog: 5 circuits, main circuit main
module main (
);

  wire clock_1_out, mod24_1_reset_geral, mod60_1_corta_em_60, mod60_2_corta_em_60;
  wire [3:0] mod24_1_saida_hora_2, mod24_1_saida_hora_un, mod60_1_saida_dec_60, mod60_1_saida_un_60,
       mod60_2_saida_dec_60, mod60_2_saida_un_60;

  Hex_Digit_Display hex_digit_display_1 (.value(mod24_1_saida_hora_2));  // open: dp
  Clock clock_1 (.out(clock_1_out));
  Hex_Digit_Display hex_digit_display_2 (.value(mod24_1_saida_hora_un));  // open: dp
  Hex_Digit_Display hex_digit_display_3 (.value(mod60_2_saida_dec_60));  // open: dp
  Hex_Digit_Display hex_digit_display_4 (.value(mod60_2_saida_un_60));  // open: dp
  Hex_Digit_Display hex_digit_display_5 (.value(mod60_1_saida_dec_60));  // open: dp
  MOD60 mod60_1 (
    .CLOCK(clock_1_out), .RESET_GERAL(mod24_1_reset_geral), .SAIDA_UN_60(mod60_1_saida_un_60),
    .SAIDA_DEC_60(mod60_1_saida_dec_60), .CORTA_EM_60(mod60_1_corta_em_60));
  MOD60 mod60_2 (
    .CLOCK(mod60_1_corta_em_60), .RESET_GERAL(mod24_1_reset_geral), .SAIDA_UN_60(mod60_2_saida_un_60),
    .SAIDA_DEC_60(mod60_2_saida_dec_60), .CORTA_EM_60(mod60_2_corta_em_60));
  MOD24 mod24_1 (
    .CLOCK(mod60_2_corta_em_60), .SAIDA_HORA_2(mod24_1_saida_hora_2), .SAIDA_HORA_UN(mod24_1_saida_hora_un),
    .RESET_GERAL(mod24_1_reset_geral));
  Hex_Digit_Display hex_digit_display_6 (.value(mod60_1_saida_un_60));  // open: dp
endmodule

module MOD10 (
  input  CLOCK,
  input  RESET_GERAL,
  output [3:0] SAIDA_UN,
  output CORTA_EM_10
);

  wire or_1_out;

  T_Flip_Flop #(.trigger("falling")) t_ff_1 (
    .T(1'b1), .clk(CLOCK), .Q(SAIDA_UN[0]), .reset(or_1_out));  // open: Qn, preset
  or or_1 (or_1_out, RESET_GERAL, CORTA_EM_10);
  T_Flip_Flop #(.trigger("falling")) t_ff_2 (
    .T(1'b1), .clk(SAIDA_UN[0]), .Q(SAIDA_UN[1]), .reset(or_1_out));  // open: Qn, preset
  T_Flip_Flop #(.trigger("falling")) t_ff_3 (
    .T(1'b1), .clk(SAIDA_UN[1]), .Q(SAIDA_UN[2]), .reset(or_1_out));  // open: Qn, preset
  and and_1 (CORTA_EM_10, SAIDA_UN[1], SAIDA_UN[3]);
  T_Flip_Flop #(.trigger("falling")) t_ff_4 (
    .T(1'b1), .clk(SAIDA_UN[2]), .Q(SAIDA_UN[3]), .reset(or_1_out));  // open: Qn, preset

  // Other names for the same wires on the sheet: Segundo_menos_significativo[3:0] = SAIDA_UN
endmodule

module MOD6 (
  input  CLOCK,
  output [3:0] SAIDA_6,
  output CORTA_EM_6
);

  T_Flip_Flop #(.trigger("falling")) t_ff_1 (
    .T(1'b1), .clk(CLOCK), .Q(SAIDA_6[0]), .reset(CORTA_EM_6));  // open: Qn, preset
  T_Flip_Flop #(.trigger("falling")) t_ff_2 (
    .T(1'b1), .clk(SAIDA_6[0]), .Q(SAIDA_6[1]), .reset(CORTA_EM_6));  // open: Qn, preset
  T_Flip_Flop #(.trigger("falling")) t_ff_3 (
    .T(1'b1), .clk(SAIDA_6[1]), .Q(SAIDA_6[2]), .reset(CORTA_EM_6));  // open: Qn, preset
  and and_1 (CORTA_EM_6, SAIDA_6[1], SAIDA_6[2]);

  assign SAIDA_6[3] = 1'b0;
endmodule

module MOD60 (
  input  CLOCK,
  input  RESET_GERAL,
  output [3:0] SAIDA_UN_60,
  output [3:0] SAIDA_DEC_60,
  output CORTA_EM_60
);

  wire mod10_1_corta_em_10;

  MOD10 mod10_1 (.CLOCK(CLOCK), .RESET_GERAL(RESET_GERAL), .SAIDA_UN(SAIDA_UN_60), .CORTA_EM_10(mod10_1_corta_em_10));
  MOD6 mod6_1 (.CLOCK(mod10_1_corta_em_10), .SAIDA_6(SAIDA_DEC_60), .CORTA_EM_6(CORTA_EM_60));
endmodule

module MOD24 (
  input  CLOCK,
  output [3:0] SAIDA_HORA_2,
  output [3:0] SAIDA_HORA_UN,
  output RESET_GERAL
);

  wire and_1_out, not_1_out, or_1_out, QUANDO_4_out, QUANDO_10_out, t_ff_1_qn, t_ff_3_qn, t_ff_4_qn;

  and and_1 (and_1_out, QUANDO_10_out, not_1_out);
  T_Flip_Flop #(.trigger("falling")) t_ff_1 (
    .T(1'b1), .clk(and_1_out), .Q(SAIDA_HORA_2[0]), .Qn(t_ff_1_qn), .reset(RESET_GERAL));  // open: preset
  not not_1 (not_1_out, RESET_GERAL);
  T_Flip_Flop #(.trigger("falling")) t_ff_2 (
    .T(1'b1), .clk(SAIDA_HORA_2[0]), .Q(SAIDA_HORA_2[1]), .reset(RESET_GERAL));  // open: Qn, preset
  and QUANDO_3 (RESET_GERAL, t_ff_1_qn, QUANDO_4_out, SAIDA_HORA_2[1]);
  T_Flip_Flop #(.trigger("falling")) t_ff_3 (
    .T(1'b1), .clk(CLOCK), .Q(SAIDA_HORA_UN[0]), .Qn(t_ff_3_qn), .reset(or_1_out));  // open: preset
  or or_1 (or_1_out, RESET_GERAL, QUANDO_10_out);
  T_Flip_Flop #(.trigger("falling")) t_ff_4 (
    .T(1'b1), .clk(SAIDA_HORA_UN[0]), .Q(SAIDA_HORA_UN[1]), .Qn(t_ff_4_qn), .reset(or_1_out));  // open: preset
  and QUANDO_4 (QUANDO_4_out, t_ff_3_qn, t_ff_4_qn, SAIDA_HORA_UN[2]);
  T_Flip_Flop #(.trigger("falling")) t_ff_5 (
    .T(1'b1), .clk(SAIDA_HORA_UN[1]), .Q(SAIDA_HORA_UN[2]), .reset(or_1_out));  // open: Qn, preset
  T_Flip_Flop #(.trigger("falling")) t_ff_6 (
    .T(1'b1), .clk(SAIDA_HORA_UN[2]), .Q(SAIDA_HORA_UN[3]), .reset(or_1_out));  // open: Qn, preset
  and QUANDO_10 (QUANDO_10_out, SAIDA_HORA_UN[1], SAIDA_HORA_UN[3]);

  assign SAIDA_HORA_2[3:2] = 2'b00;

  // Other names for the same wires on the sheet: Hora_mais_significativo[1:0] = SAIDA_HORA_2[1:0];
  //   Hora_menos_significativo[3:0] = SAIDA_HORA_UN
endmodule
