// Logisim project relogio_sequencial_sync.circ as structural Verilog: 10 circuits, main circuit main
module main (
);

  wire and_1_out, and_2_out, and_3_out, clock_1_out, mod6_1_carry, mod10_1_carry, mod10_2_carry;
  wire [1:0] MS_HOUR;
  wire [2:0] MS_MIN;
  wire [3:0] LS_HOUR, LS_MIN;

  Clock clock_1 (.out(clock_1_out));
  and and_1 (and_1_out, mod6_1_carry, mod10_1_carry);
  and and_2 (and_2_out, mod10_2_carry, and_1_out);
  MOD10 mod10_1 (
    .ENABLE(1'b1), .CLK(clock_1_out), .A3(LS_MIN[3]), .A2(LS_MIN[2]), .A1(LS_MIN[1]), .A0(LS_MIN[0]),
    .CARRY(mod10_1_carry));  // open: RESET
  MOD6 mod6_1 (
    .ENABLE(mod10_1_carry), .CLK(clock_1_out), .RESET(1'b0), .A2(MS_MIN[2]), .A1(MS_MIN[1]), .A0(MS_MIN[0]),
    .CARRY(mod6_1_carry));
  MOD10 mod10_2 (
    .ENABLE(and_1_out), .CLK(clock_1_out), .RESET(and_3_out), .A3(LS_HOUR[3]), .A2(LS_HOUR[2]),
    .A1(LS_HOUR[1]), .A0(LS_HOUR[0]), .CARRY(mod10_2_carry));
  MOD3 mod3_1 (
    .ENABLE(and_2_out), .CLK(clock_1_out), .RESET(and_3_out), .A1(MS_HOUR[1]), .A0(MS_HOUR[0]));  // open: CARRY
  Hex_Digit_Display hex_digit_display_1 (.value({2'b00, MS_HOUR}));  // open: dp
  Hex_Digit_Display hex_digit_display_2 (.value(LS_HOUR));  // open: dp
  and and_3 (and_3_out, LS_HOUR[2], MS_HOUR[1]);
  Hex_Digit_Display hex_digit_display_3 (.value({1'b0, MS_MIN}));  // open: dp
  Hex_Digit_Display hex_digit_display_4 (.value(LS_MIN));  // open: dp

  // Notes on the sheet:
  //   :
endmodule

module MOD10 (
  input  ENABLE,
  input  CLK,
  input  RESET,
  output A3,
  output A2,
  output A1,
  output A0,
  output CARRY
);

  wire and_1_out, and_2_out, and_3_out, and_4_out, and_5_out, and_6_out, and_7_out, and_8_out, not_1_out,
       not_2_out, not_3_out, not_4_out, TQ0S, TQ1S, TQ2S, TQ3S, TS0, TS1, TS2, TS3;

  not not_1 (not_1_out, ENABLE);
  and and_1 (and_1_out, A3, not_1_out);
  and and_2 (and_2_out, ENABLE, TS3);
  or or_1 (TQ3S, and_1_out, and_2_out);
  MOD10_CMB mod10_cmb_1 (.a(A3), .b(A2), .c(A1), .d(A0), .q3(TS3), .q2(TS2), .q1(TS1), .q0(TS0));
  not not_2 (not_2_out, ENABLE);
  and and_3 (and_3_out, A1, not_2_out);
  and and_4 (and_4_out, ENABLE, TS1);
  or or_2 (TQ1S, and_3_out, and_4_out);
  not not_3 (not_3_out, ENABLE);
  not not_4 (not_4_out, ENABLE);
  MOD10_SEQ mod10_seq_1 (
    .Q3(TQ3S), .Q2(TQ2S), .Q1(TQ1S), .Q0(TQ0S), .CLK(CLK), .RESET(RESET), .A(A3), .B(A2), .C(A1), .D(A0),
    .CARRY(CARRY));
  and and_5 (and_5_out, A2, not_3_out);
  and and_6 (and_6_out, ENABLE, TS2);
  and and_7 (and_7_out, A0, not_4_out);
  and and_8 (and_8_out, ENABLE, TS0);
  or or_3 (TQ2S, and_5_out, and_6_out);
  or or_4 (TQ0S, and_7_out, and_8_out);

  // Other names for the same wires on the sheet: TA = A3; TB = A2; TC = A1; TD = A0
endmodule

module MOD10_CMB (
  input  a,
  input  b,
  input  c,
  input  d,
  output q3,
  output q2,
  output q1,
  output q0
);

  wire and_1_out, and_2_out, and_3_out, and_4_out, and_5_out, and_6_out, and_7_out, and_8_out, and_9_out,
       not_1_out, not_2_out, not_3_out, not_4_out;

  not not_1 (not_1_out, a);
  not not_2 (not_2_out, b);
  not not_3 (not_3_out, c);
  not not_4 (not_4_out, d);
  and and_1 (and_1_out, not_1_out, b, c, d);
  and and_2 (and_2_out, a, not_2_out, not_3_out, not_4_out);
  and and_3 (and_3_out, not_1_out, not_2_out, c, d);
  and and_4 (and_4_out, not_1_out, b, not_3_out);
  and and_5 (and_5_out, not_1_out, b, not_4_out);
  and and_6 (and_6_out, not_1_out, not_3_out, d);
  and and_7 (and_7_out, not_1_out, c, not_4_out);
  and and_8 (and_8_out, not_1_out, not_4_out);
  and and_9 (and_9_out, not_2_out, not_3_out, not_4_out);
  or or_1 (q3, and_1_out, and_2_out);
  or or_2 (q2, and_3_out, and_4_out, and_5_out);
  or or_3 (q1, and_6_out, and_7_out);
  or or_4 (q0, and_8_out, and_9_out);
endmodule

module MOD10_SEQ (
  input  Q3,
  input  Q2,
  input  Q1,
  input  Q0,
  input  CLK,
  input  RESET,
  output A,
  output B,
  output C,
  output D,
  output CARRY
);

  D_Flip_Flop d_ff_1 (.D(Q3), .clk(CLK), .Q(A), .reset(RESET));  // open: Qn, preset
  D_Flip_Flop d_ff_2 (.D(Q2), .clk(CLK), .Q(B), .reset(RESET));  // open: Qn, preset
  D_Flip_Flop d_ff_3 (.D(Q1), .clk(CLK), .Q(C), .reset(RESET));  // open: Qn, preset
  D_Flip_Flop d_ff_4 (.D(Q0), .clk(CLK), .Q(D), .reset(RESET));  // open: Qn, preset
  and and_1 (CARRY, D, A);
endmodule

module MOD6_CMB (
  input  Q2,
  input  Q1,
  input  Q0,
  output S2,
  output S1,
  output S0
);

  wire and_1_out, and_2_out, and_3_out, and_4_out, and_5_out, and_6_out, not_1_out, not_2_out, not_3_out;

  not not_1 (not_1_out, Q2);
  not not_2 (not_2_out, Q1);
  not not_3 (not_3_out, Q0);
  and and_1 (and_1_out, not_1_out, Q1, Q0);
  and and_2 (and_2_out, Q2, not_2_out, not_3_out);
  and and_3 (and_3_out, not_1_out, not_2_out, Q0);
  and and_4 (and_4_out, not_1_out, Q1, not_3_out);
  and and_5 (and_5_out, not_1_out, not_3_out);
  and and_6 (and_6_out, not_2_out, not_3_out);
  or or_1 (S2, and_1_out, and_2_out);
  or or_2 (S1, and_3_out, and_4_out);
  or or_3 (S0, and_5_out, and_6_out);
endmodule

module MOD6_SEQ (
  input  Q2,
  input  Q1,
  input  Q0,
  input  CLK,
  input  RESET,
  output A,
  output B,
  output C,
  output CARRY
);

  D_Flip_Flop d_ff_1 (.D(Q2), .clk(CLK), .Q(A), .reset(RESET));  // open: Qn, preset
  D_Flip_Flop d_ff_2 (.D(Q1), .clk(CLK), .Q(B), .reset(RESET));  // open: Qn, preset
  D_Flip_Flop d_ff_3 (.D(Q0), .clk(CLK), .Q(C), .reset(RESET));  // open: Qn, preset
  and and_1 (CARRY, C, A);
endmodule

module MOD6 (
  input  ENABLE,
  input  CLK,
  input  RESET,
  output A2,
  output A1,
  output A0,
  output CARRY
);

  wire and_1_out, and_2_out, and_3_out, and_4_out, and_5_out, and_6_out, not_1_out, not_2_out, not_3_out,
       TQ0S, TQ1S, TQ2S, TS0, TS1, TS2;

  not not_1 (not_1_out, ENABLE);
  and and_1 (and_1_out, A2, not_1_out);
  and and_2 (and_2_out, ENABLE, TS2);
  or or_1 (TQ2S, and_1_out, and_2_out);
  MOD6_CMB mod6_cmb_1 (.Q2(A2), .Q1(A1), .Q0(A0), .S2(TS2), .S1(TS1), .S0(TS0));
  not not_2 (not_2_out, ENABLE);
  and and_3 (and_3_out, A0, not_2_out);
  and and_4 (and_4_out, ENABLE, TS0);
  or or_2 (TQ0S, and_3_out, and_4_out);
  not not_3 (not_3_out, ENABLE);
  and and_5 (and_5_out, A1, not_3_out);
  and and_6 (and_6_out, ENABLE, TS1);
  MOD6_SEQ mod6_seq_1 (
    .Q2(TQ2S), .Q1(TQ1S), .Q0(TQ0S), .CLK(CLK), .RESET(RESET), .A(A2), .B(A1), .C(A0), .CARRY(CARRY));
  or or_3 (TQ1S, and_5_out, and_6_out);

  // Other names for the same wires on the sheet: TA = A2; TB = A1; TC = A0
endmodule

module MOD3_CMB (
  input  Q1,
  input  Q0,
  output A1,
  output A0
);

  wire and_1_out, and_2_out, not_1_out;

  not not_1 (not_1_out, Q1);
  not not_2 (A0, Q0);
  and and_1 (and_1_out, not_1_out, Q0);
  and and_2 (and_2_out, Q1, A0);
  or or_1 (A1, and_1_out, and_2_out);
endmodule

module MOD3_SEQ (
  input  Q1,
  input  Q0,
  input  CLK,
  input  RESET,
  output A,
  output B,
  output CARRY
);

  wire d_ff_2_qn;

  D_Flip_Flop d_ff_1 (.D(Q1), .clk(CLK), .Q(A), .reset(RESET));  // open: Qn, preset
  D_Flip_Flop d_ff_2 (.D(Q0), .clk(CLK), .Q(B), .Qn(d_ff_2_qn), .reset(RESET));  // open: preset
  and and_1 (CARRY, A, d_ff_2_qn);
endmodule

module MOD3 (
  input  ENABLE,
  input  CLK,
  input  RESET,
  output A1,
  output A0,
  output CARRY
);

  wire and_1_out, and_2_out, and_3_out, and_4_out, not_1_out, not_2_out, TQ0S, TQ1S, TS0, TS1;

  not not_1 (not_1_out, ENABLE);
  and and_1 (and_1_out, A1, not_1_out);
  and and_2 (and_2_out, ENABLE, TS1);
  MOD3_CMB mod3_cmb_1 (.Q1(A1), .Q0(A0), .A1(TS1), .A0(TS0));
  or or_1 (TQ1S, and_1_out, and_2_out);
  not not_2 (not_2_out, ENABLE);
  and and_3 (and_3_out, A0, not_2_out);
  and and_4 (and_4_out, ENABLE, TS0);
  or or_2 (TQ0S, and_3_out, and_4_out);
  MOD3_SEQ mod3_seq_1 (.Q1(TQ1S), .Q0(TQ0S), .CLK(CLK), .RESET(RESET), .A(A1), .B(A0), .CARRY(CARRY));

  // Other names for the same wires on the sheet: TA = A1; TB = A0
endmodule
